# Fritzing sketch New_board (saved by Fritzing 0.9.3b)
circuit board: 14.5148cm x 5.9872cm
breadboards: 1

parts:
  J1 = Raspberry PI B 40-pin header [form="♂ (shrouded male)" package=THT]
  U1 = V_REG_LD1117VXX [package=78xxl]
  C1 = Ceramic Capacitor [capacitance=100nF voltage=5.5V package="100 mil [THT, multilayer]"]
  C2 = Electrolytic Capacitor [capacitance=10µF package="100 mil [THT, electrolytic]"]
  S1 = Pushbutton [package="[THT]"]
  S2 = Pushbutton [package="[THT]"]
  S3 = Pushbutton [package="[THT]"]
  S4 = Pushbutton [package="[THT]"]
  S5 = Pushbutton [package="[THT]"]
  S6 = Toggle Switch [package=THT]
  S7 = Toggle Switch [package=THT]
  LED1 = LED - 5mm [color="Red (635nm)" package="5 mm [THT]"]
  LED2 = LED - 5mm [color="Yellow (585nm)" package="5 mm [THT]"]
  LED3 = LED - 5mm [color="Green (565nm)" package="5 mm [THT]"]
  LED4 = LED - 5mm [color="Blue (430nm)" package="5 mm [THT]"]
  R1 = Resistor [tolerance=±5% resistance=35 package=THT]
  R2 = Resistor [tolerance=±5% resistance=25 package=THT]
  R3 = Resistor [tolerance=±5% resistance=35 package=THT]
  R4 = Resistor [tolerance=±5% resistance=85 package=THT]

nets:
  N1: J1.Pin_3, S3.Pin_3, S3.Pin_4
  N2: J1.Pin_5, S4.Pin_3, S4.Pin_4
  N3: J1.Pin_7, S5.Pin_3, S5.Pin_4
  N4: J1.Pin_9, S1.Pin_1, S1.Pin_2, S2.Pin_1, S2.Pin_2, S3.Pin_1, S3.Pin_2, S4.Pin_1, S4.Pin_2, S5.Pin_1, S5.Pin_2, S6.COM, S7.COM
  N5: J1.Pin_27, S1.Pin_3, S1.Pin_4
  N6: J1.Pin_29, S6.L2
  N7: J1.Pin_31, S6.L1
  N8: J1.Pin_28, S2.Pin_3
  N9: J1.Pin_26, S7.L2
  N10: J1.Pin_24, S7.L1
  N11: J1.Pin_6, U1.GND, C1.0, C2.-
  N12: J1.Pin_2, U1.IN, C1.1
  N13: U1.OUT, C2.+
  N14: LED1.cathode, R1.Pin_1
  N15: LED2.cathode, R2.Pin_1
  N16: LED3.cathode, R3.Pin_1
  N17: LED4.cathode, R4.Pin_1

notes:
  800mA out
  make pullup/down external?

custom parts:
  Raspberry PI B 40-pin header: 40-pin header for the PI 3 model B
