# Fritzing sketch New_board2 (saved by Fritzing 0.9.3b)
circuit board: 14.5148cm x 5.9872cm
breadboards: 1

parts:
  U1 = V_REG_LD1117VXX [package=78xxl]
  C1 = Ceramic Capacitor [capacitance=100nF voltage=5.5V package="100 mil [THT, multilayer]"]
  C2 = Electrolytic Capacitor [capacitance=10µF package="100 mil [THT, electrolytic]"]
  S1 = Pushbutton [package="[THT]"]
  S2 = Pushbutton [package="[THT]"]
  S3 = Pushbutton [package="[THT]"]
  S4 = Pushbutton [package="[THT]"]
  S5 = Pushbutton [package="[THT]"]
  S6 = Toggle Switch [package=THT]
  S7 = Toggle Switch [package=THT]
  LED1 = LED - 5mm [color="Red (635nm)" package="5 mm [THT]"]
  LED2 = LED - 5mm [color="Yellow (585nm)" package="5 mm [THT]"]
  LED3 = LED - 5mm [color="Green (565nm)" package="5 mm [THT]"]
  LED4 = LED - 5mm [color="Blue (430nm)" package="5 mm [THT]"]
  R1 = Resistor [tolerance=±5% resistance=35 package=THT]
  R2 = Resistor [tolerance=±5% resistance=25 package=THT]
  R3 = Resistor [tolerance=±5% resistance=35 package=THT]
  R4 = Resistor [tolerance=±5% resistance=85 package=THT]
  J1 = Raspberry PI B 40-pin header [form="♂ (shrouded male)" package=THT]
  R15 = Resistor [tolerance=±5% resistance=2.2k package=THT]
  R20 = Resistor [tolerance=±5% resistance=10k package=THT]
  R12 = Resistor [tolerance=±5% resistance=10k package=THT]
  R9 = Resistor [tolerance=±5% resistance=2.2k package=THT]
  R5 = Resistor [tolerance=±5% resistance=2.2k package=THT]
  R8 = Resistor [tolerance=±5% resistance=10k package=THT]
  R10 = Resistor [tolerance=±5% resistance=10k package=THT]
  R19 = Resistor [tolerance=±5% resistance=2.2k package=THT]
  R6 = Resistor [tolerance=±5% resistance=10k package=THT]
  R14 = Resistor [tolerance=±5% resistance=10k package=THT]
  R16 = Resistor [tolerance=±5% resistance=10k package=THT]
  R13 = Resistor [tolerance=±5% resistance=2.2k package=THT]
  R11 = Resistor [tolerance=±5% resistance=2.2k package=THT]
  R7 = Resistor [tolerance=±5% resistance=2.2k package=THT]
  R21 = Resistor [tolerance=±5% resistance=2.2k package=THT]
  R22 = Resistor [tolerance=±5% resistance=680 package=THT]
  Q1 = NPN-Transistor [package="TO92 [THT]"]

nets:
  N1: U1.OUT, C2.+, S1.Pin_1, S1.Pin_2, S2.Pin_1, S2.Pin_2, S3.Pin_1, S3.Pin_2, S4.Pin_1, S4.Pin_2, S5.Pin_1, S5.Pin_2, S6.COM, S7.COM
  N2: U1.GND, C1.0, C2.-, J1.Pin_25, J1.Pin_34, J1.Pin_30, J1.Pin_20, J1.Pin_6, R20.Pin_0, R12.Pin_0, R8.Pin_0, R10.Pin_0, R6.Pin_0, R14.Pin_0, R16.Pin_0, R22.Pin_1, Q1.E
  N3: U1.IN, C1.1, J1.Pin_4, J1.Pin_2
  N4: S1.Pin_3, S1.Pin_4, R5.Pin_1, R6.Pin_1
  N5: S2.Pin_3, S2.Pin_4, R8.Pin_1, R7.Pin_1
  N6: S3.Pin_3, S3.Pin_4, R9.Pin_1, R10.Pin_1
  N7: S4.Pin_3, S4.Pin_4, R12.Pin_1, R11.Pin_1
  N8: S5.Pin_3, S5.Pin_4, R14.Pin_1, R13.Pin_1
  N9: S6.L2, R15.Pin_1, R16.Pin_1
  N10: S7.L2, R20.Pin_1, R19.Pin_1
  N11: LED1.cathode, R1.Pin_1
  N12: LED2.cathode, R2.Pin_1
  N13: LED3.cathode, R3.Pin_1
  N14: LED4.cathode, R4.Pin_1
  N15: R1.Pin_0, Q1.C
  N16: J1.Pin_3, R9.Pin_0
  N17: J1.Pin_5, R11.Pin_0
  N18: J1.Pin_7, R13.Pin_0
  N19: J1.Pin_27, R5.Pin_0
  N20: J1.Pin_29, R15.Pin_0
  N21: J1.Pin_31, R19.Pin_0
  N22: J1.Pin_28, R7.Pin_0
  N23: J1.Pin_26, R21.Pin_0
  N24: R21.Pin_1, R22.Pin_0, Q1.B

notes:
  800mA out
  make pullup/down external?
  3.3V 50mA is shared amongst ALL pins
  Blue LED needs 5V!
  RC debounce ROUGHLY
  C = 1uF
  R1+R2 = 80K
  delay time ~ 21ms
  at 3.3V
  with diode 35975
  feed trigger 74HC14

custom parts:
  Raspberry PI B 40-pin header: 40-pin header for the PI 3 model B
