# Fritzing sketch New_board3 (saved by Fritzing 0.9.3b)
circuit board: 14.5355cm x 7.62465cm
breadboards: 1

parts:
  U1 = V_REG_LD1117VXX [package=78xxl]
  C1 = Ceramic Capacitor [capacitance=100nF voltage=5.5V package="100 mil [THT, multilayer]"]
  C2 = Electrolytic Capacitor [capacitance=10µF package="100 mil [THT, electrolytic]"]
  S1 = Pushbutton [package="[THT]"]
  S2 = Pushbutton [package="[THT]"]
  S3 = Pushbutton [package="[THT]"]
  S4 = Pushbutton [package="[THT]"]
  S5 = Pushbutton [package="[THT]"]
  S6 = Toggle Switch [package=THT]
  S7 = Toggle Switch [package=THT]
  LED1 = LED - 5mm [color="Red (635nm)" package="5 mm [THT]"]
  LED2 = LED - 5mm [color="Yellow (585nm)" package="5 mm [THT]"]
  LED3 = LED - 5mm [color="Green (565nm)" package="5 mm [THT]"]
  LED4 = LED - 5mm [color="Blue (430nm)" package="5 mm [THT]"]
  R1 = Resistor [tolerance=±5% resistance=35 package=THT]
  R2 = Resistor [tolerance=±5% resistance=25 package=THT]
  R3 = Resistor [tolerance=±5% resistance=35 package=THT]
  R4 = Resistor [tolerance=±5% resistance=85 package=THT]
  J1 = Raspberry PI B 40-pin header [form="♂ (shrouded male)" package=THT]
  R21 = Resistor [tolerance=±5% resistance=2.2k package=THT]
  R22 = Resistor [tolerance=±5% resistance=680 package=THT]
  Q1 = NPN-Transistor [package="TO92 [THT]"]
  IC1 = Hex Inverter Schmitt Trigger SN74HC14 [package="DIP (Dual Inline)"]
  IC2 = Hex Inverter Schmitt Trigger SN74HC14 [package="DIP (Dual Inline)"]
  R1_2 = Resistor [tolerance=±5% resistance=47k package=THT]
  D1 = Rectifier Diode [part_number=1N4001 package="300 mil [THT]"]
  R2_2 = Resistor [tolerance=±5% resistance=47k package=THT]
  C3 = Electrolytic Capacitor [capacitance=1µF package="100 mil [THT, electrolytic]"]
  R23 = Resistor [tolerance=±5% resistance=47k package=THT]
  R24 = Resistor [tolerance=±5% resistance=47k package=THT]
  D2 = Rectifier Diode [part_number=1N4001 package="300 mil [THT]"]
  C4 = Electrolytic Capacitor [capacitance=1µF package="100 mil [THT, electrolytic]"]
  R25 = Resistor [tolerance=±5% resistance=47k package=THT]
  R26 = Resistor [tolerance=±5% resistance=47k package=THT]
  D3 = Rectifier Diode [part_number=1N4001 package="300 mil [THT]"]
  C5 = Electrolytic Capacitor [capacitance=1µF package="100 mil [THT, electrolytic]"]
  R27 = Resistor [tolerance=±5% resistance=47k package=THT]
  R28 = Resistor [tolerance=±5% resistance=47k package=THT]
  D4 = Rectifier Diode [part_number=1N4001 package="300 mil [THT]"]
  C6 = Electrolytic Capacitor [capacitance=1µF package="100 mil [THT, electrolytic]"]
  R29 = Resistor [tolerance=±5% resistance=47k package=THT]
  R30 = Resistor [tolerance=±5% resistance=47k package=THT]
  D5 = Rectifier Diode [part_number=1N4001 package="300 mil [THT]"]
  C7 = Electrolytic Capacitor [capacitance=1µF package="100 mil [THT, electrolytic]"]
  R31 = Resistor [tolerance=±5% resistance=47k package=THT]
  R32 = Resistor [tolerance=±5% resistance=47k package=THT]
  D6 = Rectifier Diode [part_number=1N4001 package="300 mil [THT]"]
  C8 = Electrolytic Capacitor [capacitance=1µF package="100 mil [THT, electrolytic]"]
  R33 = Resistor [tolerance=±5% resistance=47k package=THT]
  R34 = Resistor [tolerance=±5% resistance=47k package=THT]
  D7 = Rectifier Diode [part_number=1N4001 package="300 mil [THT]"]
  C9 = Electrolytic Capacitor [capacitance=1µF package="100 mil [THT, electrolytic]"]
  R35 = Resistor [tolerance=±5% resistance=2.2k package=THT]
  R38 = Resistor [tolerance=±5% resistance=2.2k package=THT]
  R39 = Resistor [tolerance=±5% resistance=680 package=THT]
  Q3 = NPN-Transistor [package="TO92 [THT]"]
  R40 = Resistor [tolerance=±5% resistance=2.2k package=THT]
  R41 = Resistor [tolerance=±5% resistance=680 package=THT]
  Q4 = NPN-Transistor [package="TO92 [THT]"]
  R42 = Resistor [tolerance=±5% resistance=2.2k package=THT]
  R43 = Resistor [tolerance=±5% resistance=680 package=THT]
  Q5 = NPN-Transistor [package="TO92 [THT]"]
  7_Segment1 = 7 Segment Display  # not connected
  IC3 = IC, DIP package, 16 pins [chip_label=IC]  # not connected
  IC4 = 4011 4 x 2 Input NAND Gate, single part [part_number=4011 package="DIP (Dual Inline) [THT]"]
  S8 = Toggle Switch [package=THT]
  R44 = Resistor [tolerance=±5% resistance=220 package=THT]
  R45 = Resistor [tolerance=±5% resistance=220 package=THT]
  LED5 = LED - 5mm [color="Red (633nm)" package="5 mm [THT]"]

nets:
  N1: U1.OUT, C2.+, LED1.anode, LED2.anode, LED3.anode, R1_2.Pin_1, R23.Pin_1, R26.Pin_1, R28.Pin_1, R30.Pin_1, R32.Pin_1, R34.Pin_1, R35.Pin_1
  N2: U1.GND, C1.0, C2.-, J1.Pin_25, J1.Pin_30, J1.Pin_6, R22.Pin_0, Q1.E, R39.Pin_0, Q3.E, R41.Pin_0, Q4.E, R43.Pin_0, Q5.E
  N3: U1.IN, C1.1, LED4.anode, J1.Pin_4, J1.Pin_2
  N4: S1.Pin_1, S1.Pin_2, IC1.1A, R1_2.Pin_0, D1.anode, R2_2.Pin_1
  GND: S1.Pin_3, S1.Pin_4, S2.Pin_3, S2.Pin_4, S3.Pin_3, S3.Pin_4, S4.Pin_3, S4.Pin_4, S5.Pin_3, S5.Pin_4, S6.L1, S7.L1, IC1.GND, IC2.GND, C3.-, C4.-, C5.-, C6.-, C7.-, C8.-, C9.-
  N5: S2.Pin_1, S2.Pin_2, IC1.2A, R23.Pin_0, R24.Pin_1, D2.anode
  N6: S3.Pin_1, S3.Pin_2, IC1.3A, R25.Pin_1, R26.Pin_0, D3.anode
  N7: S4.Pin_1, S4.Pin_2, IC2.1A, R27.Pin_1, R28.Pin_0, D4.anode
  N8: S5.Pin_1, S5.Pin_2, IC2.2A, R29.Pin_1, R30.Pin_0, D5.anode
  N9: S6.COM, IC2.3A, R31.Pin_1, R32.Pin_0, D6.anode
  N10: S7.COM, IC2.4A, R33.Pin_1, R34.Pin_0, D7.anode
  N11: LED1.cathode, R1.Pin_1
  N12: LED2.cathode, R2.Pin_1
  N13: LED3.cathode, R3.Pin_1
  N14: LED4.cathode, R4.Pin_1
  N15: R1.Pin_0, Q1.C
  N16: R2.Pin_0, Q3.C
  N17: R3.Pin_0, Q4.C
  N18: R4.Pin_0, Q5.C
  N19: J1.Pin_3, IC1.3Y
  N20: J1.Pin_5, IC2.1Y
  N21: J1.Pin_7, IC2.2Y
  N22: J1.Pin_19, R42.Pin_0
  N23: J1.Pin_21, R40.Pin_0
  N24: J1.Pin_27, IC1.1Y
  N25: J1.Pin_29, IC2.3Y
  N26: J1.Pin_31, IC2.4Y
  N27: J1.Pin_28, IC1.2Y
  N28: J1.Pin_26, R21.Pin_0
  N29: J1.Pin_24, R38.Pin_0
  N30: R21.Pin_1, R22.Pin_1, Q1.B
  N31: IC1.4A, IC1.5A, IC1.6A, IC2.5A, IC2.6A
  VCC: IC1.VCC, IC2.VCC, R35.Pin_0
  N32: D1.cathode, R2_2.Pin_0, C3.+
  N33: R24.Pin_0, D2.cathode, C4.+
  N34: R25.Pin_0, D3.cathode, C5.+
  N35: R27.Pin_0, D4.cathode, C6.+
  N36: R29.Pin_0, D5.cathode, C7.+
  N37: R31.Pin_0, D6.cathode, C8.+
  N38: R33.Pin_0, D7.cathode, C9.+
  N39: R38.Pin_1, R39.Pin_1, Q3.B
  N40: R40.Pin_1, R41.Pin_1, Q4.B
  N41: R42.Pin_1, R43.Pin_1, Q5.B
  N42: IC4.A1, S8.L1, R45.Pin_0
  N43: IC4.B1, IC4.Q2
  N44: IC4.Q1, IC4.B2, LED5.anode
  N45: IC4.A2, S8.L2, R44.Pin_1
  GND_2: S8.COM
  5V: R44.Pin_0, R45.Pin_1

notes:
  800mA out
  make pullup/down external?
  3.3V 50mA is shared amongst ALL pins
  Blue LED needs 5V!
  RC debounce ROUGHLY
  C = 1uF
  R1+R2 = 80K
  delay time ~ 24ms
  at 3.3V
  with diode 35975
  feed trigger 74HC14
  ?????

custom parts:
  Raspberry PI B 40-pin header: 40-pin header for the PI 3 model B
