# Fritzing sketch Rev_B (saved by Fritzing 0.9.3b)
circuit board: 13cm x 8cm
breadboards: 1

parts:
  U1 = V_REG_LD1117VXX [package=78xxl]
  C6 = Ceramic Capacitor [capacitance=100nF voltage=5.5V package="100 mil [THT, multilayer]"]
  C7 = Electrolytic Capacitor [capacitance=10µF package="100 mil [THT, electrolytic]"]
  S1 = Pushbutton [package="[THT]"]
  S2 = Pushbutton [package="[THT]"]
  S3 = Pushbutton [package="[THT]"]
  S4 = Pushbutton [package="[THT]"]
  S5 = Pushbutton [package="[THT]"]
  S6 = Toggle Switch [package=THT]
  S7 = Toggle Switch [package=THT]
  LED1 = LED - 5mm [color="Red (635nm)" package="5 mm [THT]"]
  LED2 = LED - 5mm [color="Yellow (585nm)" package="5 mm [THT]"]
  LED3 = LED - 5mm [color="Green (565nm)" package="5 mm [THT]"]
  LED4 = LED - 5mm [color="Blue (430nm)" package="5 mm [THT]"]
  R20 = Resistor [tolerance=±5% resistance=35 package=THT]
  R21 = Resistor [tolerance=±5% resistance=25 package=THT]
  R22 = Resistor [tolerance=±5% resistance=35 package=THT]
  R23 = Resistor [tolerance=±5% resistance=22k package=THT]
  J1 = Raspberry PI B 40-pin header [form="♂ (shrouded male)" package=THT]
  R15 = Resistor [tolerance=±5% resistance=47k package=THT]
  Q1 = NPN-Transistor [package="TO92 [THT]"]
  R16 = Resistor [tolerance=±5% resistance=47k package=THT]
  Q2 = NPN-Transistor [package="TO92 [THT]"]
  R17 = Resistor [tolerance=±5% resistance=47k package=THT]
  Q3 = NPN-Transistor [package="TO92 [THT]"]
  R18 = Resistor [tolerance=±5% resistance=47k package=THT]
  Q4 = NPN-Transistor [package="TO92 [THT]"]
  CC_7-Seg = 7 Segment Display
  CD4511BC = IC, DIP package, 16 pins [chip_label=IC]
  Part1 = Adafruit ADS1115 16Bit I2C ADC [part_number="Adafruit #1085"]
  T1 = TMP36 Temperature Sensor [package="TO92 [THT]"]
  R28 = Resistor [tolerance=±5% resistance=47k package=THT]
  Q8 = LTR-301 [package=ltr-301]
  I²C = male pin header, 4 pins [form="♂ (male)"]
  ADC = male pin header, 4 pins [form="♂ (male)"]
  UART = male pin header, 4 pins [form="♂ (male)"]
  ADC_2 = male pin header, 10 pins [form="♂ (male)"]
  Q5 = NPN-Transistor [package="TO92 [THT]"]
  R19 = Resistor [tolerance=±5% resistance=47k package=THT]
  R24 = Resistor [tolerance=±5% resistance=470 package=THT]
  Q6 = NPN-Transistor [package="TO92 [THT]"]
  Q7 = NPN-Transistor [package="TO92 [THT]"]
  R25 = Resistor [tolerance=±5% resistance=47k package=THT]
  R26 = Resistor [tolerance=±5% resistance=47k package=THT]
  100Ω_NET = IC, DIP package, 16 pins [chip_label="RNET 100Ω"]
  SP1 = SPEAKER [package=pcb_mount_speaker]
  220kΩ_NET = IC, DIP package, 16 pins [chip_label="RNET 220kΩ"]
  R29 = Resistor [tolerance=±5% resistance=2.2k package=THT]
  5V = male pin header, 2 pins [form="♂ (male)"]

nets:
  3.3V: U1.OUT, C7.+, LED1.anode, LED2.anode, LED3.anode, CD4511BC.pin3, CD4511BC.pin16, Part1.VDD, R28.Pin_0, Q8.C, I²C.pin1, ADC.pin1, UART.pin1, ADC_2.pin1, R24.Pin_0, Q6.C
  GND: U1.GND, C6.0, C7.-, S1.Pin_3, S1.Pin_4, S2.Pin_3, S2.Pin_4, S3.Pin_3, S3.Pin_4, S4.Pin_3, S4.Pin_4, S5.Pin_3, S5.Pin_4, S6.COM, S7.COM, J1.Pin_9, J1.Pin_30, J1.Pin_14, J1.Pin_6, Q1.E, Q2.E, Q3.E, Q4.E, CC_7-Seg.common_cathode, CD4511BC.pin5, CD4511BC.pin8, Part1.ADDR, Part1.GND, T1.GND, I²C.pin4, ADC.pin4, UART.pin4, ADC_2.pin2, ADC_2.pin5, Q5.E, R29.Pin_0, 5V.pin2
  N1: U1.IN, C6.1, LED4.anode, J1.Pin_4, J1.Pin_2, 5V.pin1
  N2: S1.Pin_1, S1.Pin_2, 220kΩ_NET.pin13
  N3: S2.Pin_1, 220kΩ_NET.pin14
  N4: S3.Pin_1, S3.Pin_2, 220kΩ_NET.pin15
  N5: S4.Pin_1, S4.Pin_2, 220kΩ_NET.pin16
  N6: S5.Pin_1, S5.Pin_2, 220kΩ_NET.pin11
  N7: S6.L1, 220kΩ_NET.pin10
  N8: S7.L1, 220kΩ_NET.pin12
  N9: LED1.cathode, R20.Pin_1
  N10: LED2.cathode, R21.Pin_1
  N11: LED3.cathode, R22.Pin_1
  N12: LED4.cathode, R23.Pin_1
  N13: R20.Pin_0, Q1.C
  N14: R21.Pin_0, Q2.C
  N15: R22.Pin_0, Q3.C
  N16: R23.Pin_0, Q4.C
  N17: J1.Pin_3, Part1.SDA, I²C.pin2, ADC_2.pin4
  N18: J1.Pin_5, Part1.SCL, I²C.pin3, ADC_2.pin3
  N19: J1.Pin_7, Part1.ALERT, ADC_2.pin6
  N20: J1.Pin_11, CD4511BC.pin4, R26.Pin_0
  N21: J1.Pin_13, R18.Pin_0
  N22: J1.Pin_15, CD4511BC.pin1
  N23: J1.Pin_19, 220kΩ_NET.pin7
  N24: J1.Pin_21, 220kΩ_NET.pin6
  N25: J1.Pin_23, 220kΩ_NET.pin5
  N26: J1.Pin_29, 220kΩ_NET.pin4
  N27: J1.Pin_31, 220kΩ_NET.pin3
  N28: J1.Pin_33, R19.Pin_0
  N29: J1.Pin_35, R25.Pin_0
  N30: J1.Pin_37, R17.Pin_0
  N31: J1.Pin_40, CD4511BC.pin2
  N32: J1.Pin_38, CD4511BC.pin6
  N33: J1.Pin_26, 220kΩ_NET.pin2
  N34: J1.Pin_24, 220kΩ_NET.pin1
  N35: J1.Pin_22, R16.Pin_0
  N36: J1.Pin_18, R15.Pin_0
  N37: J1.Pin_16, CD4511BC.pin7
  N38: J1.Pin_10, UART.pin3
  N39: J1.Pin_8, UART.pin2
  N40: R15.Pin_1, Q1.B
  N41: R16.Pin_1, Q2.B
  N42: R17.Pin_1, Q3.B
  N43: R18.Pin_1, Q4.B
  N44: CC_7-Seg.Segment_E, 100Ω_NET.pin10
  N45: CC_7-Seg.Segment_D, 100Ω_NET.pin11
  N46: CC_7-Seg.Segment_C, 100Ω_NET.pin12
  N47: CC_7-Seg.Segment_DP, 100Ω_NET.pin9
  N48: CC_7-Seg.Segment_B, 100Ω_NET.pin13
  N49: CC_7-Seg.Segment_A, 100Ω_NET.pin14
  N50: CC_7-Seg.Segment_F, 100Ω_NET.pin16
  N51: CC_7-Seg.Segment_G, 100Ω_NET.pin15
  N52: CD4511BC.pin9, 100Ω_NET.pin7
  N53: CD4511BC.pin10, 100Ω_NET.pin6
  N54: CD4511BC.pin11, 100Ω_NET.pin5
  N55: CD4511BC.pin12, 100Ω_NET.pin4
  N56: CD4511BC.pin13, 100Ω_NET.pin3
  N57: CD4511BC.pin14, 100Ω_NET.pin2
  N58: CD4511BC.pin15, 100Ω_NET.pin1
  N59: Part1.AIN3, ADC.pin3, ADC_2.pin10
  N60: Part1.AIN2, ADC.pin2, ADC_2.pin9
  N61: Part1.AIN1, Q8.E, ADC_2.pin8, R29.Pin_1
  N62: Part1.AIN0, T1.Vout, ADC_2.pin7
  N63: T1.+Vs, R28.Pin_1
  N64: Q5.B, R19.Pin_1
  N65: Q5.C, SP1.-
  N66: R24.Pin_1, SP1.+
  N67: Q6.E, Q7.C
  N68: Q6.B, R26.Pin_1
  N69: Q7.E, 100Ω_NET.pin8
  N70: Q7.B, R25.Pin_1
  N71: 220kΩ_NET.pin8, 220kΩ_NET.pin9

notes:
  800mA out
  3.3V 50mA is shared amongst ALL pins
  Blue LED needs 5V!
  Super goddamn bright
  2.2K is close, but could go a bit dimmer. 4.7k ?
  Lol more like 20k
  Tie GPCLK0 to the red LED as well? Speaker? TOGGLE SWITCH???
  UART
  3.3V
  TXD
  RXD
  GND
  3.3V
  SDA
  SCL
  GND
  3.3V
  AIN2
  AIN3
  GND
  jumpers next to AINs for gnd?
  ADDR -> GND
  I2C address 0x48
  NO IDEA HOW TO WIRE THIS
  Capacitor???
  3.3V
  A2
  A3
  GND
  TX
  RX
  SCL
  SDA
  Probably 100
  5V

custom parts:
  Raspberry PI B 40-pin header: 40-pin header for the PI 3 model B
  Adafruit ADS1115 16Bit I2C ADC: For microcontrollers without an analog-to-digital converter or when you want a higher-precision ADC, the ADS1115 provides 16-bit precision at 860 samples/second over I2C. The chip can be configured as 4 single-ended input channels, or two differential channels. As a nice bonus, it even includes a programmable gain amplifier, up to x16, to help boost up smaller single/differential signals to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
