# Fritzing sketch Rev_E (saved by Fritzing 0.9.3b)
circuit board: 13cm x 8cm
breadboards: 1

parts:
  U1 = V_REG_LD1117VXX [package=78xxl]
  C6 = Ceramic Capacitor [capacitance=100nF voltage=5.5V package="100 mil [THT, multilayer]"]
  C7 = Electrolytic Capacitor [capacitance=10µF package="100 mil [THT, electrolytic]"]
  S1 = Pushbutton [package="[THT]"]
  S2 = Pushbutton [package="[THT]"]
  S3 = Pushbutton [package="[THT]"]
  S4 = Pushbutton [package="[THT]"]
  S5 = Pushbutton [package="[THT]"]
  S6 = Toggle Switch [package=THT]
  S7 = Toggle Switch [package=THT]
  LED1 = LED - 5mm [color="Red (635nm)" package="5 mm [THT]"]
  LED2 = LED - 5mm [color="Yellow (585nm)" package="5 mm [THT]"]
  LED3 = LED - 5mm [color="Green (565nm)" package="5 mm [THT]"]
  LED4 = LED - 5mm [color="Blue (430nm)" package="5 mm [THT]"]
  R20 = Resistor [tolerance=±5% resistance=35 package=THT]
  R21 = Resistor [tolerance=±5% resistance=25 package=THT]
  R22 = Resistor [tolerance=±5% resistance=35 package=THT]
  R23 = Resistor [tolerance=±5% resistance=22k package=THT]
  J1 = Raspberry PI B 40-pin header [form="♂ (shrouded male)" package=THT]
  R15 = Resistor [tolerance=±5% resistance=47k package=THT]
  Q1 = NPN-Transistor [package="TO92 [THT]"]
  MM74HC14 = Hex Inverter Schmitt Trigger SN74HC14 [package="DIP (Dual Inline)"]
  R1 = Resistor [tolerance=±5% resistance=47k package=THT]
  D1 = Rectifier Diode [part_number=1N4001 package="300 mil [THT]"]
  R2 = Resistor [tolerance=±5% resistance=47k package=THT]
  C1 = Electrolytic Capacitor [capacitance=1µF package="100 mil [THT, electrolytic]"]
  R3 = Resistor [tolerance=±5% resistance=47k package=THT]
  R4 = Resistor [tolerance=±5% resistance=47k package=THT]
  D2 = Rectifier Diode [part_number=1N4001 package="300 mil [THT]"]
  C2 = Electrolytic Capacitor [capacitance=1µF package="100 mil [THT, electrolytic]"]
  R6 = Resistor [tolerance=±5% resistance=47k package=THT]
  R5 = Resistor [tolerance=±5% resistance=47k package=THT]
  D3 = Rectifier Diode [part_number=1N4001 package="300 mil [THT]"]
  C3 = Electrolytic Capacitor [capacitance=1µF package="100 mil [THT, electrolytic]"]
  R8 = Resistor [tolerance=±5% resistance=47k package=THT]
  R7 = Resistor [tolerance=±5% resistance=47k package=THT]
  D4 = Rectifier Diode [part_number=1N4001 package="300 mil [THT]"]
  C4 = Electrolytic Capacitor [capacitance=1µF package="100 mil [THT, electrolytic]"]
  R10 = Resistor [tolerance=±5% resistance=47k package=THT]
  R9 = Resistor [tolerance=±5% resistance=47k package=THT]
  D5 = Rectifier Diode [part_number=1N4001 package="300 mil [THT]"]
  C5 = Electrolytic Capacitor [capacitance=1µF package="100 mil [THT, electrolytic]"]
  R16 = Resistor [tolerance=±5% resistance=47k package=THT]
  Q2 = NPN-Transistor [package="TO92 [THT]"]
  R17 = Resistor [tolerance=±5% resistance=47k package=THT]
  Q3 = NPN-Transistor [package="TO92 [THT]"]
  R18 = Resistor [tolerance=±5% resistance=47k package=THT]
  Q4 = NPN-Transistor [package="TO92 [THT]"]
  CC_7-Seg = 7 Segment Display
  CD4511BC = IC, DIP package, 16 pins [chip_label=IC]
  R11 = Resistor [tolerance=±5% resistance=220k package=THT]
  R12 = Resistor [tolerance=±5% resistance=220k package=THT]
  R14 = Resistor [tolerance=±5% resistance=220k package=THT]
  R13 = Resistor [tolerance=±5% resistance=220k package=THT]
  CD4011 = 4011 4 x 2 Input NAND Gate, single part [part_number=4011 package="DIP (Dual Inline) [THT]"]
  Q8 = LTR-301 [package=ltr-301]
  ADC = male pin header, 4 pins [form="♂ (male)"]
  UART = male pin header, 4 pins [form="♂ (male)"]
  Q5 = NPN-Transistor [package="TO92 [THT]"]
  R24 = Resistor [tolerance=±5% resistance=470 package=THT]
  Q6 = NPN-Transistor [package="TO92 [THT]"]
  Q7 = NPN-Transistor [package="TO92 [THT]"]
  R25 = Resistor [tolerance=±5% resistance=47k package=THT]
  R26 = Resistor [tolerance=±5% resistance=47k package=THT]
  100Ω_NET = IC, DIP package, 16 pins [chip_label="RNET 100Ω"]
  SP1 = SPEAKER [package=pcb_mount_speaker]
  47kΩ_NET = IC, DIP package, 16 pins [chip_label="RNET 100Ω"]
  5V = male pin header, 2 pins [form="♂ (male)"]
  C8 = Ceramic Capacitor [capacitance=100nF package="100 mil [THT, multilayer]"]
  R29 = Resistor [tolerance=±5% resistance=10k package=THT]
  R19 = Resistor [tolerance=±5% resistance=47k package=THT]
  MCP3004 = IC, DIP package, 14 pins [chip_label=MCP3004]
  SPI_0_1 = male pin header, 6 pins [form="♂ (male)"]
  C9 = Ceramic Capacitor [capacitance=100nF package="100 mil [THT, multilayer]"]
  C10 = Ceramic Capacitor [capacitance=100nF package="100 mil [THT, multilayer]"]
  POT1 = TRIMPOT [package=trimpot_pth_s3_lock]
  ADC_GND = male pin header, 2 pins [form="♂ (male)"]

nets:
  3.3V: U1.OUT, C7.+, LED1.anode, LED2.anode, LED3.anode, MM74HC14.VCC, R1.Pin_1, R3.Pin_1, R5.Pin_1, R7.Pin_1, R9.Pin_1, CD4511BC.pin3, CD4511BC.pin16, R11.Pin_1, R12.Pin_1, R14.Pin_1, R13.Pin_1, CD4011.VDD, Q8.C, ADC.pin1, UART.pin1, R24.Pin_0, Q6.C, C8.1, MCP3004.pin13, MCP3004.pin14, SPI_0_1.pin1, C9.1, C10.1, POT1.CCW
  GND: U1.GND, C6.0, C7.-, S1.Pin_3, S1.Pin_4, S2.Pin_3, S2.Pin_4, S3.Pin_3, S3.Pin_4, S4.Pin_3, S4.Pin_4, S5.Pin_3, S5.Pin_4, S6.COM, S7.COM, J1.Pin_9, J1.Pin_39, J1.Pin_30, J1.Pin_14, J1.Pin_6, Q1.E, MM74HC14.GND, MM74HC14.6A, C1.-, C2.-, C3.-, C4.-, C5.-, Q2.E, Q3.E, Q4.E, CC_7-Seg.common_cathode, CD4511BC.pin5, CD4511BC.pin8, CD4011.GND, ADC.pin4, UART.pin4, Q5.E, 5V.pin2, C8.0, R29.Pin_0, MCP3004.pin5, MCP3004.pin6, MCP3004.pin7, MCP3004.pin12, SPI_0_1.pin2, C9.0, C10.0, POT1.CW, ADC_GND.pin1, ADC_GND.pin2
  N1: U1.IN, C6.1, LED4.anode, J1.Pin_4, J1.Pin_2, 5V.pin1
  N2: S1.Pin_1, S1.Pin_2, MM74HC14.2A, R1.Pin_0, D1.anode, R2.Pin_1
  N3: S2.Pin_1, S2.Pin_2, MM74HC14.1A, R3.Pin_0, R4.Pin_1, D2.anode
  N4: S3.Pin_1, S3.Pin_2, MM74HC14.3A, R6.Pin_1, R5.Pin_0, D3.anode
  N5: S4.Pin_1, S4.Pin_2, MM74HC14.5A, R8.Pin_1, R7.Pin_0, D4.anode
  N6: S5.Pin_1, S5.Pin_2, MM74HC14.4A, R10.Pin_1, R9.Pin_0, D5.anode
  N7: S6.L1, R11.Pin_0, CD4011.B1
  N8: S6.L2, R12.Pin_0, CD4011.B2
  N9: S7.L1, R13.Pin_0, CD4011.B4
  N10: S7.L2, R14.Pin_0, CD4011.A3
  N11: LED1.cathode, R20.Pin_1
  N12: LED2.cathode, R21.Pin_1
  N13: LED3.cathode, R22.Pin_1
  N14: LED4.cathode, R23.Pin_1
  N15: R20.Pin_0, Q1.C
  N16: R21.Pin_0, Q2.C
  N17: R22.Pin_0, Q3.C
  N18: R23.Pin_0, Q4.C
  N19: J1.Pin_3, 47kΩ_NET.pin8
  N20: J1.Pin_5, 47kΩ_NET.pin7
  N21: J1.Pin_7, 47kΩ_NET.pin6
  N22: J1.Pin_11, CD4511BC.pin4, R26.Pin_0
  N23: J1.Pin_13, R18.Pin_0
  N24: J1.Pin_15, CD4511BC.pin1
  N25: J1.Pin_19, MCP3004.pin9, SPI_0_1.pin6
  N26: J1.Pin_21, MCP3004.pin10, SPI_0_1.pin5
  N27: J1.Pin_23, MCP3004.pin11, SPI_0_1.pin4
  N28: J1.Pin_29, 47kΩ_NET.pin5
  N29: J1.Pin_31, 47kΩ_NET.pin4
  N30: J1.Pin_33, 47kΩ_NET.pin1
  N31: J1.Pin_35, R25.Pin_0
  N32: J1.Pin_37, R17.Pin_0
  N33: J1.Pin_40, CD4511BC.pin2
  N34: J1.Pin_38, CD4511BC.pin6
  N35: J1.Pin_36, R19.Pin_0
  N36: J1.Pin_32, 47kΩ_NET.pin2
  N37: J1.Pin_26, SPI_0_1.pin3
  N38: J1.Pin_24, MCP3004.pin8
  N39: J1.Pin_22, R16.Pin_0
  N40: J1.Pin_18, R15.Pin_0
  N41: J1.Pin_16, CD4511BC.pin7
  N42: J1.Pin_10, UART.pin3
  N43: J1.Pin_8, UART.pin2
  N44: R15.Pin_1, Q1.B
  N45: MM74HC14.1Y, 47kΩ_NET.pin10
  N46: MM74HC14.2Y, 47kΩ_NET.pin9
  N47: MM74HC14.3Y, 47kΩ_NET.pin11
  N48: MM74HC14.4Y, 47kΩ_NET.pin13
  N49: MM74HC14.5Y, 47kΩ_NET.pin12
  N50: D1.cathode, R2.Pin_0, C1.+
  N51: R4.Pin_0, D2.cathode, C2.+
  N52: R6.Pin_0, D3.cathode, C3.+
  N53: R8.Pin_0, D4.cathode, C4.+
  N54: R10.Pin_0, D5.cathode, C5.+
  N55: R16.Pin_1, Q2.B
  N56: R17.Pin_1, Q3.B
  N57: R18.Pin_1, Q4.B
  N58: CC_7-Seg.Segment_E, 100Ω_NET.pin10
  N59: CC_7-Seg.Segment_D, 100Ω_NET.pin11
  N60: CC_7-Seg.Segment_C, 100Ω_NET.pin12
  N61: CC_7-Seg.Segment_DP, 100Ω_NET.pin9
  N62: CC_7-Seg.Segment_B, 100Ω_NET.pin13
  N63: CC_7-Seg.Segment_A, 100Ω_NET.pin14
  N64: CC_7-Seg.Segment_F, 100Ω_NET.pin16
  N65: CC_7-Seg.Segment_G, 100Ω_NET.pin15
  N66: CD4511BC.pin9, 100Ω_NET.pin7
  N67: CD4511BC.pin10, 100Ω_NET.pin6
  N68: CD4511BC.pin11, 100Ω_NET.pin5
  N69: CD4511BC.pin12, 100Ω_NET.pin4
  N70: CD4511BC.pin13, 100Ω_NET.pin3
  N71: CD4511BC.pin14, 100Ω_NET.pin2
  N72: CD4511BC.pin15, 100Ω_NET.pin1
  N73: CD4011.A1, CD4011.Q2
  N74: CD4011.Q1, CD4011.A2, 47kΩ_NET.pin15
  N75: CD4011.B3, CD4011.Q4, 47kΩ_NET.pin16
  N76: CD4011.Q3, CD4011.A4
  N77: Q8.E, R29.Pin_1, MCP3004.pin1
  N78: ADC.pin2, MCP3004.pin4
  N79: ADC.pin3, MCP3004.pin3
  N80: Q5.B, R19.Pin_1
  N81: Q5.C, SP1.-
  N82: R24.Pin_1, SP1.+
  N83: Q6.E, Q7.C
  N84: Q6.B, R26.Pin_1
  N85: Q7.E, 100Ω_NET.pin8
  N86: Q7.B, R25.Pin_1
  N87: 47kΩ_NET.pin3, 47kΩ_NET.pin14
  N88: MCP3004.pin2, POT1.WIPER

notes:
  800mA out
  3.3V 50mA is shared amongst ALL pins
  Blue LED needs 5V!
  Super goddamn bright
  2.2K is close, but could go a bit dimmer. 4.7k ?
  Lol more like 20k
  RC debounce ROUGHLY
  C = 1uF
  R1+R2 = 80K
  delay time ~ 24ms
  at 3.3V
  with diode 35975
  feed trigger 74HC14
  Tie GPCLK0 to the red LED as well? Speaker? TOGGLE SWITCH???
  UART
  3.3V
  TXD
  RXD
  GND
  3.3V
  GND
  CE1
  SCLK
  MISO
  MOSI
  3.3V
  AIN3
  AIN2
  GND
  NO IDEA HOW TO WIRE THIS
  Capacitor???
  3.3V
  A2
  A3
  GND
  TX
  RX
  Probably 100
  5V
  SLCK
  CE1
  MOSI
  MISO

custom parts:
  Raspberry PI B 40-pin header: 40-pin header for the PI 3 model B
