# Fritzing sketch Rev_F (saved by Fritzing 0.9.3b)
circuit board: 13cm x 8cm
breadboards: 1

parts:
  LD1117V33 = V_REG_LD1117VXX [package=78xxl]
  C7 = Ceramic Capacitor [capacitance=100nF voltage=5.5V package="100 mil [THT, multilayer]"]
  C6 = Electrolytic Capacitor [capacitance=10µF package="100 mil [THT, electrolytic]"]
  S1 = Pushbutton [package="[THT]"]
  S2 = Pushbutton [package="[THT]"]
  S3 = Pushbutton [package="[THT]"]
  S4 = Pushbutton [package="[THT]"]
  S5 = Pushbutton [package="[THT]"]
  LED1 = LED - 5mm [color="Red (635nm)" package="5 mm [THT]"]
  LED2 = LED - 5mm [color="Yellow (585nm)" package="5 mm [THT]"]
  LED3 = LED - 5mm [color="Green (565nm)" package="5 mm [THT]"]
  LED4 = LED - 5mm [color="Blue (430nm)" package="5 mm [THT]"]
  R20 = Resistor [tolerance=±5% resistance=35 package=THT]
  R21 = Resistor [tolerance=±5% resistance=25 package=THT]
  R22 = Resistor [tolerance=±5% resistance=35 package=THT]
  R23 = Resistor [tolerance=±5% resistance=22k package=THT]
  R15 = Resistor [tolerance=±5% resistance=47k package=THT]
  Q1 = NPN-Transistor [package="TO92 [THT]"]
  74HC14N = Hex Inverter Schmitt Trigger SN74HC14 [package="DIP (Dual Inline)"]
  R1 = Resistor [tolerance=±5% resistance=47k package=THT]
  D1 = Rectifier Diode [part_number=1N4148FS package="300 mil [THT]"]
  R2 = Resistor [tolerance=±5% resistance=47k package=THT]
  C1 = Electrolytic Capacitor [capacitance=1µF package="100 mil [THT, electrolytic]"]
  R3 = Resistor [tolerance=±5% resistance=47k package=THT]
  R4 = Resistor [tolerance=±5% resistance=47k package=THT]
  D2 = Rectifier Diode [part_number=1N4148FS package="300 mil [THT]"]
  C2 = Electrolytic Capacitor [capacitance=1µF package="100 mil [THT, electrolytic]"]
  R6 = Resistor [tolerance=±5% resistance=47k package=THT]
  R5 = Resistor [tolerance=±5% resistance=47k package=THT]
  D3 = Rectifier Diode [part_number=1N4148FS package="300 mil [THT]"]
  C3 = Electrolytic Capacitor [capacitance=1µF package="100 mil [THT, electrolytic]"]
  R8 = Resistor [tolerance=±5% resistance=47k package=THT]
  R7 = Resistor [tolerance=±5% resistance=47k package=THT]
  D4 = Rectifier Diode [part_number=1N4148FS package="300 mil [THT]"]
  C4 = Electrolytic Capacitor [capacitance=1µF package="100 mil [THT, electrolytic]"]
  R10 = Resistor [tolerance=±5% resistance=47k package=THT]
  R9 = Resistor [tolerance=±5% resistance=47k package=THT]
  D5 = Rectifier Diode [part_number=1N4148FS package="300 mil [THT]"]
  R16 = Resistor [tolerance=±5% resistance=47k package=THT]
  R17 = Resistor [tolerance=±5% resistance=47k package=THT]
  Q3 = NPN-Transistor [package="TO92 [THT]"]
  R18 = Resistor [tolerance=±5% resistance=47k package=THT]
  Q4 = NPN-Transistor [package="TO92 [THT]"]
  CC_7-Seg = 7 Segment Display
  CD4511 = IC, DIP package, 16 pins [chip_label=IC]
  R11 = Resistor [tolerance=±5% resistance=220k package=THT]
  R12 = Resistor [tolerance=±5% resistance=220k package=THT]
  R14 = Resistor [tolerance=±5% resistance=220k package=THT]
  R13 = Resistor [tolerance=±5% resistance=220k package=THT]
  CD4011 = 4011 4 x 2 Input NAND Gate, single part [part_number=4011 package="DIP (Dual Inline) [THT]"]
  ADC = male pin header, 4 pins [form="♂ (male)"]
  UART = male pin header, 4 pins [form="♂ (male)"]
  Q5 = NPN-Transistor [package="TO92 [THT]"]
  R24 = Resistor [tolerance=±5% resistance=220 package=THT]
  Q6 = NPN-Transistor [package="TO92 [THT]"]
  Q7 = NPN-Transistor [package="TO92 [THT]"]
  R25 = Resistor [tolerance=±5% resistance=47k package=THT]
  R26 = Resistor [tolerance=±5% resistance=47k package=THT]
  100Ω_NET = IC, DIP package, 16 pins [chip_label="RNET 100Ω"]
  5V = male pin header, 2 pins [form="♂ (male)"]
  C9 = Ceramic Capacitor [capacitance=100nF package="100 mil [THT, multilayer]"]
  R19 = Resistor [tolerance=±5% resistance=47k package=THT]
  MCP3004 = IC, DIP package, 14 pins [chip_label=MCP3004]
  SPI_0_1 = male pin header, 6 pins [form="♂ (male)"]
  C8 = Ceramic Capacitor [capacitance=100nF package="100 mil [THT, multilayer]"]
  C12 = Ceramic Capacitor [capacitance=100nF package="100 mil [THT, multilayer]"]
  ADC_GND = male pin header, 2 pins [form="♂ (male)"]
  J1 = Raspberry PI B 40-pin header [form="♂ (shrouded male)" package=THT]
  C13 = Ceramic Capacitor [capacitance=100nF package="100 mil [THT, multilayer]"]
  Q8 = LED - 5mm [color="White (4500K)" package="5 mm [THT]"]
  POT1 = TRIMPOT [package=3386u]
  R27 = Resistor [tolerance=±5% resistance=220k package=THT]
  R28 = Resistor [tolerance=±5% resistance=330 package=THT]
  Q2 = NPN-Transistor [package="TO92 [THT]"]
  C10 = Ceramic Capacitor [capacitance=100nF package="100 mil [THT, multilayer]"]
  C11 = Ceramic Capacitor [capacitance=100nF package="100 mil [THT, multilayer]"]
  C14 = Ceramic Capacitor [capacitance=100nF package="100 mil [THT, multilayer]"]
  S7 = SPST Switch [package=switch-spdt]
  S8 = SPST Switch [package=switch-spdt]
  C5 = Electrolytic Capacitor [capacitance=1µF package="100 mil [THT, electrolytic]"]
  47kΩ_NET = IC, DIP package, 16 pins [chip_label="RNET 47kΩ"]
  C15 = Ceramic Capacitor [capacitance=100nF package="100 mil [THT, multilayer]"]
  C16 = Ceramic Capacitor [capacitance=100nF package="100 mil [THT, multilayer]"]
  C17 = Ceramic Capacitor [capacitance=100nF package="100 mil [THT, multilayer]"]
  C18 = Ceramic Capacitor [capacitance=1µF package="100 mil [THT, multilayer]"]  # not connected
  C19 = Ceramic Capacitor [capacitance=1µF package="100 mil [THT, multilayer]"]  # not connected
  D6 = Rectifier Diode [part_number=1N4148FS package="300 mil [THT]"]
  D7 = Rectifier Diode [part_number=1N4148FS package="300 mil [THT]"]
  SP1 = SPEAKER [package=pcb_mount_speaker]
  J3 = female pin header, 3 pins [form="♀ (female)"]
  J4 = female pin header, 3 pins [form="♀ (female)"]
  J2 = female pin header, 1 pin [form="♀ (female)"]

nets:
  3.3V: LD1117V33.OUT, C6.+, LED1.anode, LED2.anode, LED3.anode, 74HC14N.VCC, R1.Pin_1, R3.Pin_1, R5.Pin_1, R7.Pin_1, R9.Pin_1, CD4511.pin3, CD4511.pin16, R11.Pin_1, R12.Pin_1, R14.Pin_1, R13.Pin_1, CD4011.VDD, ADC.pin1, UART.pin1, Q6.C, MCP3004.pin13, SPI_0_1.pin1, C8.1, C12.1, Q8.anode, R28.Pin_0, C15.1, C16.1, C17.1
  GND: LD1117V33.GND, C7.0, C6.-, S1.Pin_3, S1.Pin_4, S2.Pin_3, S2.Pin_4, S3.Pin_3, S3.Pin_4, S4.Pin_3, S4.Pin_4, S5.Pin_3, S5.Pin_4, Q1.E, 74HC14N.GND, 74HC14N.6A, C1.-, C2.-, C3.-, C4.-, Q3.E, Q4.E, CC_7-Seg.common_cathode, CD4511.pin5, CD4511.pin8, CD4011.GND, ADC.pin4, UART.pin4, 5V.pin2, C9.0, MCP3004.pin5, MCP3004.pin6, MCP3004.pin7, MCP3004.pin12, SPI_0_1.pin2, C12.0, ADC_GND.pin1, ADC_GND.pin2, J1.Pin_9, J1.Pin_39, J1.Pin_30, J1.Pin_14, J1.Pin_6, C13.0, POT1.CW, R27.Pin_0, Q2.E, C10.0, C11.0, C14.0, S7.P, S8.P, C5.-, C15.0, C16.0, C17.0, SP1.-, J3.pin3, J4.pin3
  5V: LD1117V33.IN, C7.1, LED4.anode, R24.Pin_0, 5V.pin1, MCP3004.pin14, J1.Pin_4, J1.Pin_2, C13.1
  N1: S1.Pin_1, S1.Pin_2, 74HC14N.1A, R1.Pin_0, D1.anode, R2.Pin_1
  N2: S2.Pin_1, S2.Pin_2, 74HC14N.2A, R3.Pin_0, R4.Pin_1, D2.anode
  N3: S3.Pin_1, S3.Pin_2, 74HC14N.3A, R6.Pin_1, R5.Pin_0, D3.anode
  N4: S4.Pin_1, S4.Pin_2, 74HC14N.5A, R8.Pin_1, R7.Pin_0, D4.anode
  N5: S5.Pin_1, S5.Pin_2, 74HC14N.4A, R10.Pin_1, R9.Pin_0, D5.anode
  N6: LED1.cathode, R20.Pin_1
  N7: LED2.cathode, R21.Pin_1
  N8: LED3.cathode, R22.Pin_1
  N9: LED4.cathode, R23.Pin_1
  N10: R20.Pin_0, Q1.C
  N11: R21.Pin_0, Q2.C
  N12: R22.Pin_0, Q3.C
  N13: R23.Pin_0, Q4.C
  N14: R15.Pin_0, J1.Pin_3
  N15: R15.Pin_1, Q1.B
  N16: 74HC14N.1Y, 47kΩ_NET.pin5
  N17: 74HC14N.2Y, 47kΩ_NET.pin1
  N18: 74HC14N.3Y, 47kΩ_NET.pin2
  N19: 74HC14N.4Y, 47kΩ_NET.pin4
  N20: 74HC14N.5Y, 47kΩ_NET.pin3
  N21: D1.cathode, R2.Pin_0, C1.+
  N22: R4.Pin_0, D2.cathode, C2.+
  N23: R6.Pin_0, D3.cathode, C3.+
  N24: R8.Pin_0, D4.cathode, C4.+
  N25: R10.Pin_0, D5.cathode, C5.+
  N26: R16.Pin_0, J1.Pin_5
  N27: R16.Pin_1, Q2.B
  N28: R17.Pin_0, J1.Pin_7
  N29: R17.Pin_1, Q3.B
  N30: R18.Pin_0, J1.Pin_29
  N31: R18.Pin_1, Q4.B
  N32: CC_7-Seg.Segment_E, 100Ω_NET.pin10
  N33: CC_7-Seg.Segment_D, 100Ω_NET.pin11
  N34: CC_7-Seg.Segment_C, 100Ω_NET.pin12
  N35: CC_7-Seg.Segment_DP, 100Ω_NET.pin9
  N36: CC_7-Seg.Segment_B, 100Ω_NET.pin13
  N37: CC_7-Seg.Segment_A, 100Ω_NET.pin14
  N38: CC_7-Seg.Segment_F, 100Ω_NET.pin16
  N39: CC_7-Seg.Segment_G, 100Ω_NET.pin15
  N40: CD4511.pin1, J1.Pin_22
  N41: CD4511.pin2, J1.Pin_37
  N42: CD4511.pin4, R26.Pin_0, J1.Pin_40
  N43: CD4511.pin6, J1.Pin_13
  N44: CD4511.pin7, J1.Pin_18
  N45: CD4511.pin9, 100Ω_NET.pin7
  N46: CD4511.pin10, 100Ω_NET.pin6
  N47: CD4511.pin11, 100Ω_NET.pin5
  N48: CD4511.pin12, 100Ω_NET.pin4
  N49: CD4511.pin13, 100Ω_NET.pin3
  N50: CD4511.pin14, 100Ω_NET.pin2
  N51: CD4511.pin15, 100Ω_NET.pin1
  N52: R11.Pin_0, CD4011.B1, S8.O
  N53: R12.Pin_0, CD4011.B2, S8.S
  N54: R14.Pin_0, CD4011.A3, S7.S
  N55: R13.Pin_0, CD4011.B4, S7.O
  N56: CD4011.A1, CD4011.Q2
  N57: CD4011.Q1, CD4011.A2, D6.anode
  N58: CD4011.B3, CD4011.Q4, D7.anode
  N59: CD4011.Q3, CD4011.A4
  N60: ADC.pin2, MCP3004.pin4, C11.1
  N61: ADC.pin3, MCP3004.pin3, C10.1
  N62: UART.pin2, J1.Pin_8
  N63: UART.pin3, J1.Pin_10
  N64: Q5.E, SP1.+, J2.pin1
  N65: Q5.B, R19.Pin_1, C14.1
  N66: Q5.C, R24.Pin_1
  N67: Q6.E, Q7.C
  N68: Q6.B, R26.Pin_1
  N69: Q7.E, 100Ω_NET.pin8
  N70: Q7.B, R25.Pin_1
  N71: R25.Pin_0, J1.Pin_16
  N72: C9.1, MCP3004.pin2, POT1.WIPER, J3.pin2, J4.pin2
  N73: R19.Pin_0, J1.Pin_31
  N74: MCP3004.pin1, C8.0, Q8.cathode, R27.Pin_1
  N75: MCP3004.pin8, J1.Pin_24
  N76: MCP3004.pin9, SPI_0_1.pin6, J1.Pin_19
  N77: MCP3004.pin10, SPI_0_1.pin5, J1.Pin_21
  N78: MCP3004.pin11, SPI_0_1.pin4, J1.Pin_23
  N79: SPI_0_1.pin3, J1.Pin_26
  N80: J1.Pin_11, 47kΩ_NET.pin16
  N81: J1.Pin_33, 47kΩ_NET.pin9
  N82: J1.Pin_35, 47kΩ_NET.pin14
  N83: J1.Pin_38, 47kΩ_NET.pin13
  N84: J1.Pin_36, 47kΩ_NET.pin12
  N85: J1.Pin_32, 47kΩ_NET.pin10
  N86: J1.Pin_12, 47kΩ_NET.pin15
  N87: POT1.CCW, R28.Pin_1, J3.pin1, J4.pin1
  N88: 47kΩ_NET.pin6, 47kΩ_NET.pin11
  N89: 47kΩ_NET.pin7, D6.cathode
  N90: 47kΩ_NET.pin8, D7.cathode

notes:
  800mA out
  3.3V 50mA is shared amongst ALL pins
  RC debounce ROUGHLY
  C = 1uF
  R1+R2 = 80K
  delay time ~ 24ms
  at 3.3V
  with diode 35975
  feed trigger 74HC14
  Tie GPCLK0 to the red LED as well? Speaker? TOGGLE SWITCH???
  UART
  3.3V
  TXD
  RXD
  GND
  3.3V
  GND
  CE1
  SCLK
  MISO
  MOSI
  3.3V
  AIN3
  AIN2
  GND
  3.3V
  A2
  A3
  GND
  TX
  RX
  Probably 100
  5V
  SLCK
  CE1
  MOSI
  MISO
  Extras for alt pin spacing
  5V for higher clock
  LED silkscreen more accurate
  500Hz
  ~20kHz
  Will Starms 2017 v1.5
  +
  10kHz-3.6MHz
  Update parts list
  cap count & type
  R24 value
  Diode across speaker
  - -> + ?
  Pin spacing for 17.5mm speakers

custom parts:
  Raspberry PI B 40-pin header: 40-pin header for the PI 3 model B
